# Fritzing sketch Fritzing sketch (saved by Fritzing 0.9.5d)
breadboards: 1

parts:
  WeMos_D1_Mini1 = WeMos D1 Mini
  WeMos_D1_Mini_Battery_Shield1 = WeMos D1 Mini Battery Shield
  WeMos_D1_Mini_Motor_Shield1 = WeMos D1 Mini Motor Shield
  M1 = DC Motor
  M2 = DC Motor
  BAT1 = Battery Holders [package=battery-aa-kit]
  P1 = S1133 Si Photodiode [package="8mm Ceramic [THT]"]
  P2 = S1133 Si Photodiode [package="8mm Ceramic [THT]"]
  HC-SR04_Sensor_1 = HC-SR04 Ultrasonic Distance Sensor
  U1 = SWITCH_SPDT [package=kps-1290]

nets:
  5V: WeMos_D1_Mini1.5V, WeMos_D1_Mini_Battery_Shield1.5V, WeMos_D1_Mini_Motor_Shield1.5V, HC-SR04_Sensor_1.VCC
  N1: WeMos_D1_Mini1.D0, P1.anode
  N2: WeMos_D1_Mini1.D1, WeMos_D1_Mini_Motor_Shield1.D1
  N3: WeMos_D1_Mini1.D2, WeMos_D1_Mini_Motor_Shield1.D2
  N4: WeMos_D1_Mini1.D5, HC-SR04_Sensor_1.ECHO
  N5: WeMos_D1_Mini1.D6, HC-SR04_Sensor_1.TRIG
  N6: WeMos_D1_Mini1.D7, WeMos_D1_Mini_Battery_Shield1.3V3
  N7: WeMos_D1_Mini1.D8, P2.anode
  N8: WeMos_D1_Mini1.G, WeMos_D1_Mini_Battery_Shield1.G, WeMos_D1_Mini_Motor_Shield1.G, P1.cathode, P2.cathode, HC-SR04_Sensor_1.GND
  N9: WeMos_D1_Mini_Motor_Shield1.A1, M1.pin_2
  N10: WeMos_D1_Mini_Motor_Shield1.A2, M1.pin_1
  N11: WeMos_D1_Mini_Motor_Shield1.B1, M2.pin_1
  N12: WeMos_D1_Mini_Motor_Shield1.B2, M2.pin_2
  N13: BAT1.+, U1.O
